# Fritzing sketch wiring (saved by Fritzing 0.9.6b)
perfboards: 1

parts:
  J1 = JST XH_2.54mm Horizontal SMD_Connector 2pin [package=SMD]
  DFPlayer_Mini1 = DFPlayer MINI [package="DIP (Dual Inline) [THT]"]
  A1 = Waveshare rp2040-zero tht [package=THT]
  J2 = JST XH_2.54mm Horizontal SMD Connector 3pin [package=SMD]
  J3 = JST XH_2.54mm Horizontal SMD Connector 3pin [package=SMD]
  J4 = JST XH_2.54mm Horizontal SMD_Connector 2pin [package=SMD]
  J5 = JST XH_2.54mm Horizontal SMD_Connector 2pin [package=SMD]
  J6 = JST XH_2.54mm Horizontal SMD Connector 3pin [package=SMD]
  CONN1 = USB connector [package=THT]
  TRS1 = Audio Jack (TRS) 3.5mm [package="4Ucon 08780 [THT]"]
  J7 = JST XH_2.54mm Horizontal SMD Connector 3pin [package=SMD]
  Part1 = ws2812b [package="smd 2812b"]

nets:
  5V: J1.pin1, A1.Pin_2, CONN1.5V, J7.pin1, Part1.VSS
  N1: J1.pin2, A1.Pin_1, CONN1.d+, J7.pin2, Part1.VDD
  N2: DFPlayer_Mini1.RX, A1.Pin_19
  N3: DFPlayer_Mini1.TX, A1.Pin_18
  N4: DFPlayer_Mini1.DAC_R, J6.pin1, TRS1.Ring
  N5: DFPlayer_Mini1.DAC_L, J6.pin2, TRS1.Tip
  N6: A1.Pin_3, J2.pin2, J3.pin2, J4.pin1, J5.pin1
  N7: A1.Pin_5, J7.pin3, Part1.DIN
  N8: J2.pin1, J3.pin1
  N9: J2.pin3, J3.pin3, J4.pin2, J5.pin2, J6.pin3, TRS1.Sleeve

notes:
  USB Power
  2 (or more) connectors to beam receiver / sender
  external status neo pixel LED
  Audio Jack

custom parts:
  JST XH_2.54mm Horizontal SMD_Connector 2pin: JST XH_2.54mm Horizontal SMD_Connector 2pin.
  DFPlayer MINI: MP3 module by DFRobot.com for playing Music from an SD-Card. Supports WAV and MP3 files.
  Waveshare rp2040-zero tht: .RP2040-Zero, A Low-Cost, High-Performance Pico-Like MCU Board Based On Raspberry Pi Microcontroller RP2040. This varant is THT without the extra connections.
  JST XH_2.54mm Horizontal SMD Connector 3pin: JST XH_2.54mm Horizontal SMD Connector 3pin.
